# Fritzing sketch circuit schematic (saved by Fritzing 0.9.3b)
breadboards: 1

parts:
  GLCD_128x1 = 128 x 64 Graphic LCD
  Part1 = Arduino Uno (Rev3)
  S1 = Pushbutton [package="[THT]"]
  S2 = Pushbutton [package="[THT]"]
  S3 = Pushbutton [package="[THT]"]
  S4 = Pushbutton [package="[THT]"]
  R1 = Rotary Potentiometer (Small) [maximum_resistance=100kΩ package=THT]
  R2 = Resistor [tolerance=±5% resistance=220 package=THT]
  R4 = Resistor [tolerance=±5% resistance=220 package=THT]
  R5 = Resistor [tolerance=±5% resistance=220 package=THT]
  R6 = Resistor [tolerance=±5% resistance=220 package=THT]

nets:
  N1: GLCD_128x1.1_Vss, GLCD_128x1.20_K(-), Part1.GND, R1.wiper, R2.Pin_0, R4.Pin_0, R5.Pin_0, R6.Pin_0
  N2: GLCD_128x1.2_Vdd, GLCD_128x1.19_A(+), Part1.5V
  N3: GLCD_128x1.3_Vo, R1.leg2
  N4: GLCD_128x1.4_D/I, Part1.A3
  N5: GLCD_128x1.5_R/W, Part1.A2
  N6: GLCD_128x1.6_Enable, Part1.A4/SDA
  N7: GLCD_128x1.7_DB0, Part1.D8
  N8: GLCD_128x1.8_DB1, Part1.D9_PWM
  N9: GLCD_128x1.9_BD2, Part1.D10_PWM/SS
  N10: GLCD_128x1.10_DB3, Part1.D11_PWM/MOSI
  N11: GLCD_128x1.11_DB4, Part1.D4
  N12: GLCD_128x1.12_DB5, Part1.D5_PWM
  N13: GLCD_128x1.13_DB6, Part1.D6_PWM
  N14: GLCD_128x1.14_DB7, Part1.D7
  N15: GLCD_128x1.15_CS1, Part1.A0
  N16: GLCD_128x1.16_CS2, Part1.A1
  N17: GLCD_128x1.17_RST, Part1.RESET
  N18: GLCD_128x1.18_Vout, R1.leg1
  N19: Part1.D12/MISO, S2.Pin_3, S2.Pin_4, R5.Pin_1
  N20: Part1.D13/SCK, S3.Pin_3, S3.Pin_4, R6.Pin_1
  N21: Part1.D2, S1.Pin_3, S1.Pin_4, R2.Pin_1
  N22: Part1.D3_PWM, S4.Pin_3, S4.Pin_4, R4.Pin_1
  N23: S1.Pin_1, S1.Pin_2
  N24: S2.Pin_1, S2.Pin_2
  N25: S3.Pin_1, S3.Pin_2
  N26: S4.Pin_1, S4.Pin_2
